# Fritzing sketch Smart Moneybag (saved by Fritzing 0.8.7b)
circuit board: 4.31136cm x 5.25364cm

parts:
  CNY70-1 = CNY70 [package=cny70-side]
  R1 = Resistor [tolerance=±5% resistance=220 package=THT]
  Q1 = NPN-Transistor [package="TO92 [THT]"]
  R2 = Resistor [tolerance=±5% resistance=10k package=THT]
  S2 = Pushbutton [package="[THT]"]
  J1 = Piezo Speaker
  LED1 = LED - 5mm [color="Red (633nm)" package="5 mm [THT]"]
  R3 = Resistor [tolerance=±5% resistance=1k package=THT]
  Arduino_Pro_Mini = Arduino Pro Mini v13

nets:
  N1: CNY70-1.A, R1.Pin_0
  N2: CNY70-1.C, CNY70-1.K, S2.Pin_3, S2.Pin_4, J1.pin1, LED1.cathode, Arduino_Pro_Mini.GND
  N3: CNY70-1.E, R2.Pin_1, Arduino_Pro_Mini.A0
  N4: R1.Pin_1, Q1.E
  N5: Q1.B, R3.Pin_1
  N6: Q1.C, R2.Pin_0, Arduino_Pro_Mini.VCC
  N7: S2.Pin_1, S2.Pin_2, Arduino_Pro_Mini.D2
  N8: J1.pin2, Arduino_Pro_Mini.D6_PWM
  N9: LED1.anode, Arduino_Pro_Mini.D13/SCK
  N10: R3.Pin_0, Arduino_Pro_Mini.A1

custom parts:
  CNY70: PHOTOTRANSISTOR
